# Fritzing sketch Schematics (saved by Fritzing 0.9.3b)
breadboards: 1

parts:
  Part1 = Arduino Uno (Rev3) - ICSP
  U1 = LCD-16X2 [package=lcd-16x2_noholes]
  J1 = Piezo Speaker
  Part2 = Real Time Clock Module - DS1307 RTC Breakout Board
  R1 = Resistor [tolerance=±5% resistance=220 package=THT]
  S1 = Pushbutton [package="[THT]"]
  S2 = Pushbutton [package="[THT]"]
  S3 = Pushbutton [package="[THT]"]

nets:
  N1: Part1.A0, S1.Pin_3, S1.Pin_4
  N2: Part1.A4/SDA, Part2.SDA
  N3: Part1.A5/SCL, Part2.SCL
  5V: Part1.5V, U1.VDD, Part2.5V
  N4: Part1.ICSP_MOSI, Part1.D11_PWM/MOSI, U1.E
  GND: Part1.GND, U1.VSS, U1.R_W, U1.K, J1.pin1, Part2.GND, S1.Pin_1, S1.Pin_2, S2.Pin_1, S2.Pin_2, S3.Pin_3, S3.Pin_4
  N5: Part1.D8, S3.Pin_1, S3.Pin_2
  N6: Part1.D9_PWM, U1.VO
  N7: Part1.D10_PWM/SS, R1.Pin_0
  N8: Part1.D12/MISO, U1.RS
  N9: Part1.D2, U1.DB7
  N10: Part1.D3_PWM, U1.DB6
  N11: Part1.D4, U1.DB5
  N12: Part1.D5_PWM, U1.DB4
  N13: Part1.D6_PWM, J1.pin2
  N14: Part1.D7, S2.Pin_3, S2.Pin_4
  N15: U1.A, R1.Pin_1
